# Fritzing sketch fritzing (saved by Fritzing 0.9.6b)
breadboards: 1

parts:
  U1 = ESP32-38PinWide [part_number=ESP32-38PinWide]
  Part1 = InvenSense MPU6050
  Part2 = InvenSense MPU6050
  Part3 = InvenSense MPU6050
  R1 = Resistor [tolerance=±5% power=0.25 resistance=1.8k package=THT]
  R2 = Resistor [tolerance=±5% power=0.25 resistance=1.8k package=THT]
  R3 = Resistor [tolerance=±5% power=0.25 resistance=1.8k package=THT]
  R4 = Resistor [tolerance=±5% power=0.25 resistance=1.8k package=THT]
  Part6 = InvenSense MPU6050

nets:
  VCC: U1.3.3, Part1.VCC, Part2.VCC, Part2.AD0, Part3.VCC, R1.Pin_0, R2.Pin_0, R3.Pin_0, R4.Pin_0, Part6.VCC
  N1: U1.GPIO36, Part1.INT
  N2: U1.GPIO39, Part3.INT
  N3: U1.GPIO34, Part6.INT
  N4: U1.GPIO35, Part2.INT
  GND: U1.GND, Part1.GND, Part2.GND, Part3.GND, Part3.AD0, Part6.GND
  N5: U1.GPIO0, Part3.SCL, Part3.SDA, R4.Pin_1, Part6.SCL
  N6: U1.GPIO4, R3.Pin_1, Part6.SDA
  N7: U1.GPIO22, Part1.SCL, Part2.SCL, R2.Pin_1
  N8: U1.GPIO23, Part1.SDA, Part2.SDA, R1.Pin_1

custom parts:
  ESP32-38PinWide: Generic 38-Pin ESP32 with wide format (only access to one side of pins on a breadboard) based on Stephen Lilley's HiLetgo ESP-WROOM-32 ESP32 ESP-32S Development Board.
